# Fritzing sketch coursework fzz (saved by Fritzing 0.9.3b)

parts:
  Часть1 = Arduino Uno (Rev3)
  J1 = Basic Servo
  Часть2 = Real Time Clock Module - DS1307 RTC Breakout Board

nets:
  N1: Часть1.A4/SDA, Часть2.SDA
  N2: Часть1.A5/SCL, Часть2.SCL
  N3: Часть1.D10_PWM/SS, J1.gnd
  GND: Часть1.GND, J1.pulse, Часть2.GND
  5V: Часть1.5V, J1.vcc, Часть2.5V
